# Fritzing sketch ESP32_SCT013_DS18B20 (saved by Fritzing 0.9.4)

parts:
  U2 = ESP 32 DEVKIT DOIT
  DS1 = DS18B20 1-Wire Temperature Sensor [part_number=DS18B20]
  SCT013_30A/1V = Inductor [package="1206 [SMD]"]
  R1 = Resistor [tolerance=±5% resistance=10k package=THT]
  R2 = Resistor [tolerance=±5% resistance=47k package=THT]
  C1 = Electrolytic Capacitor [capacitance=47µF package="100 mil [THT, electrolytic]"]
  R3 = Resistor [tolerance=±5% resistance=47k package=THT]

nets:
  N1: U2.D34, SCT013_30A/1V.pin_0
  N2: DS1.GND, C1.-, R3.Pin_1
  N3: DS1.DQ, R1.Pin_1
  N4: DS1.VDD, R1.Pin_0
  N5: SCT013_30A/1V.pin_1, R2.Pin_1, C1.+, R3.Pin_0
